# Fritzing sketch Timerv2 (saved by Fritzing 0.9.3b)
perfboards: 1

parts:
  U1 = atmega328 [package=dip]
  J1 = female pin header, 5 pins [form="♀ (female)"]  # not connected
  J2 = female pin header, 6 pins [form="♀ (female)"]  # not connected
  J3 = female pin header, 5 pins [form="♀ (female)"]  # not connected
  J4 = female pin header, 4 pins [form="♀ (female)"]  # not connected
  JP1 = Header 2 [package=jst-2-pth]  # not connected
  S1 = Pushbutton [package="[THT]"]
  Y1 = CRYSTAL [package=hc49up]
  C1 = Capacitor [package=cap-pth-small2]
  C2 = Capacitor [package=cap-pth-small2]
  R1 = Resistor [tolerance=±5% resistance=220 package="0402 [SMD]"]
  U2 = 7-SEGMENT-4DIGIT [package=7-segment-4digit-youngsun]  # not connected

nets:
  N1: U1.D9_(PWM), S1.Pin_1, S1.Pin_2
  N2: S1.Pin_3, S1.Pin_4, R1.Pin_0
  N3: Y1.1, C1.1
  N4: Y1.2, C2.1
  N5: C1.2, C2.2
